# Fritzing sketch Non-inv HPAmp (saved by Fritzing 0.9.2b)
breadboards: 1

parts:
  IC1 = Dual Op-Amp [package=dip08]
  R1 = Resistor [tolerance=±5% resistance=100k package=THT]
  C1 = Ceramic Capacitor [capacitance=100nF package="100 mil [THT, multilayer]"]
  C2 = Ceramic Capacitor [capacitance=100nF package="100 mil [THT, multilayer]"]
  R2 = Resistor [tolerance=±5% resistance=100k package=THT]
  R3 = Rotary Potentiometer (Small) [maximum_resistance=100kΩ package=THT]
  R4 = Rotary Potentiometer (Small) [maximum_resistance=100kΩ package=THT]
  R5 = Resistor [tolerance=±5% resistance=22k package=THT]
  R6 = Resistor [tolerance=±5% resistance=47k package=THT]
  R7 = Resistor [tolerance=±5% resistance=22k package=THT]
  R8 = Resistor [tolerance=±5% resistance=47k package=THT]
  TRS1 = Audio Jack (TRS) 3.5mm [package="4Ucon 08780 [THT]"]
  TRS2 = Audio Jack (TRS) 3.5mm [package="4Ucon 08780 [THT]"]
  TRS3 = Audio Jack (TRS) 3.5mm [package="4Ucon 08780 [THT]"]
  C3 = Ceramic Capacitor [capacitance=100nF package="100 mil [THT, multilayer]"]
  U1 = mystery part, 3 pins [chip_label=TLE2426]
  C4 = Electrolytic Capacitor [capacitance=1µF package="100 mil [THT, electrolytic]"]
  C5 = Electrolytic Capacitor [capacitance=1µF package="100 mil [THT, electrolytic]"]
  R9 = Resistor [tolerance=±5% resistance=4.7k package=THT]
  LED1 = LED - 3mm [color="Blue (525nm)" package="3 mm [THT]"]
  C6 = Ceramic Capacitor [capacitance=100nF package="100 mil [THT, multilayer]"]
  R10 = Resistor [tolerance=±5% resistance=22 package=THT]
  R11 = Resistor [tolerance=±5% resistance=22 package=THT]

nets:
  N1: IC1.A_OUT, R8.Pin_0, R10.Pin_1
  N2: IC1.A_-IN, R7.Pin_0, R8.Pin_1
  N3: IC1.A_+IN, R1.Pin_0, C1.0
  N4: IC1.A_V-, R2.Pin_0, R3.leg1, R4.leg1, R5.Pin_0, TRS1.Sleeve, TRS2.Sleeve, C3.1, U1.pin1, U1.pin2, C4.-, C5.-, LED1.cathode, C6.0
  N5: IC1.B_+IN, C2.0, R2.Pin_1
  N6: IC1.B_-IN, R5.Pin_1, R6.Pin_1
  N7: IC1.B_OUT, R6.Pin_0, R11.Pin_1
  N8: IC1.A_V+, C3.0, U1.pin3, C4.+, R9.Pin_0
  N9: R1.Pin_1, R7.Pin_1, C5.+, C6.1
  N10: C1.1, R4.wiper
  N11: C2.1, R3.wiper
  N12: R3.leg2, TRS3.Ring
  N13: R4.leg2, TRS3.Tip
  N14: TRS1.Ring, TRS2.Ring, R11.Pin_0
  N15: TRS1.Tip, TRS2.Tip, R10.Pin_0
  N16: R9.Pin_1, LED1.anode

notes:
  V-
  GND
  GND
  V+
